// Logisim project Guess The Number XTREME.circ as structural Verilog: 12 circuits, main circuit main
module main (
  input  in_1,
  input  in_2,
  input  in_3,
  input  in_4,
  input  in_5,
  input  in_6,
  input  in_7,
  input  in_8
);

  wire ACERTOU, and_1_out, CHUTANDO_X, CHUTANDO_Y, CHUTAR, CLK_CRONO, cronometro_1_end, cronometro_2_end,
       d_ff_1_q, d_ff_2_q, dm, dma_t, dmb_t, ds, dsa_t, dsb_t, ESTADO, flip_flop_t_1_q, flip_flop_t_2_q,
       MODO, not_1_out, not_2_out, or_1_out, or_2_out, or_3_out, or_4_out, or_5_out, or_6_out, RESET, SALVAR,
       START, SX, SY, TROCAR, tunnel, tunnel_t, tunnel_t_t, TURNO_A, TURNO_B, um, uma_t, umb_t, us, usa_t,
       usb_t;
  wire [3:0] decode_comp2_1_out_5, decode_comp2_2_out_5, DMA, DMB, DSA, DSB, MAGIC_X, MAGIC_Y, NUM_A, NUM_B,
       NX, NY, PLACAR_A, PLACAR_B, UMA, UMB, USA, USB, XCHUTE, YCHUTE;

  Button button_1 (.out(dma_t));
  Hex_Digit_Display hex_digit_display_1 (.value(DMA));  // open: dp
  Button button_2 (.out(uma_t));
  Hex_Digit_Display hex_digit_display_2 (.value(UMA));  // open: dp
  LED SA (.in(in_1));
  Hex_Digit_Display hex_digit_display_3 (.value(decode_comp2_1_out_5));  // open: dp
  decode_comp2 decode_comp2_1 (.A3(in_1), .A2(in_2), .A1(in_3), .A0(in_4), .out_6(NUM_A), .out_5(decode_comp2_1_out_5));
  Clock clock_1 (.out(CLK_CRONO));
  decode_coordenada decode_coordenada_1 (.Q(flip_flop_t_1_q), .X(CHUTANDO_X), .Y(CHUTANDO_Y));
  flip_flop_T flip_flop_t_1 (.D(or_1_out), .Q(flip_flop_t_1_q));  // open: Q_prime, CLEAR
  or or_1 (or_1_out, TROCAR, SALVAR);
  Hex_Digit_Display hex_digit_display_4 (.value(PLACAR_A));  // open: dp
  Button button_3 (.out(dsa_t));
  Hex_Digit_Display hex_digit_display_5 (.value(DSA));  // open: dp
  Button button_4 (.out(usa_t));
  Hex_Digit_Display hex_digit_display_6 (.value(USA));  // open: dp
  LED JOGA_A (.in(TURNO_A));
  LED X (.in(CHUTANDO_X));
  chuteXY chutexy_1 (
    .CHUTEA(NUM_A), .CLK(SALVAR), .SELETOR_COO(flip_flop_t_1_q), .X(NX), .Y(NY),
    .SELETOR_JOG(flip_flop_t_2_q), .CHUTEB(NUM_B), .XS(SX), .YS(SY), .XCOMP2(XCHUTE), .YCOMP2(YCHUTE));
  decode_jogador decode_jogador_1 (.Q(flip_flop_t_2_q), .J_A(TURNO_A), .J_B(TURNO_B));
  flip_flop_T flip_flop_t_2 (.D(CHUTAR), .Q(flip_flop_t_2_q));  // open: Q_prime, CLEAR
  Button u_START (.out(START));
  LED A_VENCEU ();  // open: in
  LED \MODO_EDIÇÃO  (.in(ESTADO));
  LED MAIOR (.in(tunnel_t_t));
  Button u_TROCAR (.out(TROCAR));
  LED u_SX (.in(SX));
  Hex_Digit_Display hex_digit_display_7 (.value(NX));  // open: dp
  LED FIM_DE_JOGO ();  // open: in
  LED EMPATE ();  // open: in
  LED u_ACERTOU (.in(ACERTOU));
  LED IGUAL (.in(tunnel_t));
  LED MENOR (.in(tunnel));
  LED u_SY (.in(SY));
  Button u_SALVAR (.out(SALVAR));
  LED B_VENCEU ();  // open: in
  Button CONFIGURAR (.out(MODO));
  Button u_RESET (.out(RESET));
  Button u_CHUTAR (.out(CHUTAR));
  Hex_Digit_Display hex_digit_display_8 (.value(NY));  // open: dp
  comparador comparador_1 (
    .CHUTE_X(XCHUTE), .CHUTE_Y(YCHUTE), .X(MAGIC_X), .Y(MAGIC_Y), .CLK(CHUTAR), .IGUAL(ACERTOU),
    .SOMA_MAIOR(tunnel_t_t), .SOMA_IGUAL(tunnel_t), .SOMA_MENOR(tunnel));
  coordenadas coordenadas_1 (.RESET(START), .X(MAGIC_X), .Y(MAGIC_Y));
  or or_2 (or_2_out, MODO, and_1_out);
  and and_1 (and_1_out, ESTADO, START);
  LED Y (.in(CHUTANDO_Y));
  flip_flop_T flip_flop_t_3 (.D(or_2_out), .Q(ESTADO));  // open: Q_prime, CLEAR
  Button button_5 (.out(umb_t));
  Button button_6 (.out(dmb_t));
  Hex_Digit_Display hex_digit_display_9 (.value(DMB));  // open: dp
  Hex_Digit_Display hex_digit_display_10 (.value(UMB));  // open: dp
  LED JOGA_B (.in(TURNO_B));
  Hex_Digit_Display hex_digit_display_11 (.value(PLACAR_B));  // open: dp
  Button button_7 (.out(dsb_t));
  Hex_Digit_Display hex_digit_display_12 (.value(DSB));  // open: dp
  LED SB (.in(in_5));
  Hex_Digit_Display hex_digit_display_13 (.value(decode_comp2_2_out_5));  // open: dp
  decode_comp2 decode_comp2_2 (.A3(in_5), .A2(in_6), .A1(in_7), .A0(in_8), .out_6(NUM_B), .out_5(decode_comp2_2_out_5));
  or or_3 (or_3_out, d_ff_1_q, not_1_out);
  or or_4 (or_4_out, d_ff_2_q, not_2_out);
  Button button_8 (.out(usb_t));
  Hex_Digit_Display hex_digit_display_14 (.value(USB));  // open: dp
  Cronometro cronometro_1 (
    .CLK(CLK_CRONO), .PAUSE(or_3_out), .CLEAR(RESET), .END(cronometro_1_end), .DM(DMA), .UM(UMA), .DS(DSA),
    .US(USA), .IDM(dm), .IDS(ds), .MODE(ESTADO), .IUM(um), .IUS(us));
  not not_1 (not_1_out, TURNO_A);
  Cronometro cronometro_2 (
    .CLK(CLK_CRONO), .PAUSE(or_4_out), .CLEAR(RESET), .END(cronometro_2_end), .DM(DMB), .UM(UMB), .DS(DSB),
    .US(USB), .IDM(dm), .IDS(ds), .MODE(ESTADO), .IUM(um), .IUS(us));
  not not_2 (not_2_out, TURNO_B);
  or or_5 (or_5_out, cronometro_1_end, ESTADO);
  or or_6 (or_6_out, cronometro_2_end, ESTADO);
  D_Flip_Flop d_ff_1 (.Q(d_ff_1_q), .preset(or_5_out), .reset(START));  // open: clk, D, Qn, en
  D_Flip_Flop d_ff_2 (.Q(d_ff_2_q), .preset(or_6_out), .reset(START));  // open: clk, D, Qn, en
  or or_7 (dm, dma_t, dmb_t);
  or or_8 (um, uma_t, umb_t);
  or or_9 (ds, dsb_t, dsa_t);
  or or_10 (us, usa_t, usb_t);

  // Other names for the same wires on the sheet: modo_t = ESTADO
endmodule

module Cronometro (
  input  CLK,
  input  PAUSE,
  input  CLEAR,
  input  MODE,
  input  IDM,
  input  IUM,
  input  IDS,
  input  IUS,
  output END,
  output [3:0] DM,
  output [3:0] UM,
  output [3:0] DS,
  output [3:0] US
);

  wire and_1_out, and_2_out, and_3_out, and_4_out, and_5_out, and_6_out, and_7_out, and_9_out, and_10_out,
       and_11_out, and_12_out, and_13_out, comparator_1_eq, comparator_2_eq, comparator_3_eq,
       comparator_4_eq, decsm_2_vai1, not_1_out, not_2_out, not_3_out, not_4_out, not_5_out, not_6_out,
       not_7_out, not_8_out, not_9_out, not_10_out, not_11_out, not_12_out, or_1_out, or_2_out, or_3_out,
       or_4_out, or_5_out, or_6_out, or_7_out, unitsm_1_vai1, unitsm_2_vai1;
  wire [3:0] adder_1_out, decsm_1_s0, decsm_2_s0, subtractor_1_out, subtractor_2_out, subtractor_3_out,
       unitsm_1_s0, unitsm_2_s0;

  and and_1 (and_1_out, CLK, ~PAUSE, ~MODE);  // AND_Gate
  Register #(.width(4)) register_1 (.D(decsm_1_s0), .Q(DM), .clk(or_1_out), .clr(CLEAR));  // open: en
  or or_1 (or_1_out, and_1_out, and_2_out);
  and and_2 (and_2_out, MODE, and_3_out);
  and and_3 (and_3_out, not_1_out, IDM);
  not not_1 (not_1_out, not_2_out);
  not not_2 (not_2_out, not_3_out);
  not not_3 (not_3_out, IDM);
  decSM decsm_1 (
    .A3(subtractor_1_out[3]), .A2(subtractor_1_out[2]), .A1(subtractor_1_out[1]), .A0(subtractor_1_out[0]),
    .S3(decsm_1_s0[3]), .S2(decsm_1_s0[2]), .S1(decsm_1_s0[1]), .S0(decsm_1_s0[0]));  // open: VAI1
  Subtractor #(.width(4)) subtractor_1 (.a(DM), .b(4'b0000), .out(subtractor_1_out), .bin(or_2_out));  // open: bout
  and and_4 (and_4_out, unitsm_1_vai1, ~MODE);  // AND_Gate
  or or_2 (or_2_out, and_4_out, MODE);
  or or_3 (or_3_out, and_1_out, and_5_out);
  and and_5 (and_5_out, MODE, and_6_out);
  and and_6 (and_6_out, not_4_out, IUM);
  not not_4 (not_4_out, not_5_out);
  not not_5 (not_5_out, not_6_out);
  not not_6 (not_6_out, IUM);
  unitSM unitsm_1 (
    .A3(subtractor_2_out[3]), .A2(subtractor_2_out[2]), .A1(subtractor_2_out[1]), .A0(subtractor_2_out[0]),
    .S3(unitsm_1_s0[3]), .S2(unitsm_1_s0[2]), .S1(unitsm_1_s0[1]), .S0(unitsm_1_s0[0]), .VAI1(unitsm_1_vai1));
  Register #(.width(4)) register_2 (.D(unitsm_1_s0), .Q(UM), .clk(or_3_out), .clr(CLEAR));  // open: en
  and and_7 (and_7_out, decsm_2_vai1, ~MODE);  // AND_Gate
  or or_4 (or_4_out, and_7_out, MODE);
  Subtractor #(.width(4)) subtractor_2 (.a(UM), .b(4'b0000), .out(subtractor_2_out), .bin(or_4_out));  // open: bout
  Comparator #(.width(4)) comparator_1 (.a(DM), .b(4'b0000), .eq(comparator_1_eq));  // open: gt, lt
  Comparator #(.width(4)) comparator_2 (.a(UM), .b(4'b0000), .eq(comparator_2_eq));  // open: gt, lt
  Comparator #(.width(4)) comparator_3 (.a(DS), .b(4'b0000), .eq(comparator_3_eq));  // open: gt, lt
  Comparator #(.width(4)) comparator_4 (.a(US), .b(4'b0000), .eq(comparator_4_eq));  // open: gt, lt
  or or_5 (or_5_out, and_1_out, and_9_out);
  and and_8 (END, comparator_1_eq, comparator_2_eq, comparator_3_eq, comparator_4_eq);
  decSM decsm_2 (
    .A3(subtractor_3_out[3]), .A2(subtractor_3_out[2]), .A1(subtractor_3_out[1]), .A0(subtractor_3_out[0]),
    .S3(decsm_2_s0[3]), .S2(decsm_2_s0[2]), .S1(decsm_2_s0[1]), .S0(decsm_2_s0[0]), .VAI1(decsm_2_vai1));
  Register #(.width(4)) register_3 (.D(decsm_2_s0), .Q(DS), .clk(or_5_out), .clr(CLEAR));  // open: en
  and and_9 (and_9_out, MODE, and_10_out);
  and and_10 (and_10_out, not_7_out, IDS);
  not not_7 (not_7_out, not_8_out);
  not not_8 (not_8_out, not_9_out);
  not not_9 (not_9_out, IDS);
  Subtractor #(.width(4)) subtractor_3 (.a(DS), .b(4'b0000), .out(subtractor_3_out), .bin(or_6_out));  // open: bout
  and and_11 (and_11_out, unitsm_2_vai1, ~MODE);  // AND_Gate
  or or_6 (or_6_out, and_11_out, MODE);
  Register #(.width(4)) register_4 (.D(unitsm_2_s0), .Q(US), .clk(or_7_out), .clr(CLEAR));  // open: en
  or or_7 (or_7_out, and_1_out, and_12_out);
  and and_12 (and_12_out, MODE, and_13_out);
  and and_13 (and_13_out, not_10_out, IUS);
  not not_10 (not_10_out, not_11_out);
  not not_11 (not_11_out, not_12_out);
  not not_12 (not_12_out, IUS);
  unitSM unitsm_2 (
    .A3(adder_1_out[3]), .A2(adder_1_out[2]), .A1(adder_1_out[1]), .A0(adder_1_out[0]), .S3(unitsm_2_s0[3]),
    .S2(unitsm_2_s0[2]), .S1(unitsm_2_s0[1]), .S0(unitsm_2_s0[0]), .VAI1(unitsm_2_vai1));
  Adder #(.width(4)) adder_1 (.a(4'b1111), .b(US), .out(adder_1_out));  // open: cin, cout
endmodule

module unitSM (
  input  A3,
  input  A2,
  input  A1,
  input  A0,
  output S3,
  output S2,
  output S1,
  output S0,
  output VAI1
);

  wire and_1_out, and_2_out, and_3_out, and_4_out, and_5_out, and_6_out, and_7_out, and_8_out, and_9_out,
       and_10_out, and_11_out, not_1_out, not_2_out, not_3_out, not_4_out, not_5_out, not_6_out, not_7_out,
       not_8_out;

  not not_1 (not_1_out, A3);
  not not_2 (not_2_out, A0);
  not not_3 (not_3_out, A3);
  not not_4 (not_4_out, A2);
  not not_5 (not_5_out, A0);
  not not_6 (not_6_out, A3);
  not not_7 (not_7_out, A2);
  not not_8 (not_8_out, A0);
  and and_1 (and_1_out, A3, A1);
  and and_2 (and_2_out, A3, A2);
  and and_3 (and_3_out, not_1_out, A2);
  or or_1 (S2, and_3_out, and_4_out);
  and and_4 (and_4_out, A2, not_2_out);
  and and_5 (and_5_out, not_3_out, A1);
  and and_6 (and_6_out, not_4_out, A1);
  or or_2 (S1, and_5_out, and_6_out, and_7_out);
  and and_7 (and_7_out, A1, not_5_out);
  and and_8 (and_8_out, not_6_out, A0);
  and and_9 (and_9_out, not_7_out, A0);
  and and_10 (and_10_out, A1, A0);
  and and_11 (and_11_out, A3, A2, not_8_out);
  or or_3 (VAI1, and_1_out, and_2_out);
  or or_4 (S0, and_8_out, and_9_out, and_10_out, and_11_out);

  assign S3 = A3;
endmodule

module decSM (
  input  A3,
  input  A2,
  input  A1,
  input  A0,
  output S3,
  output S2,
  output S1,
  output S0,
  output VAI1
);

  wire and_1_out, and_2_out, and_3_out, and_4_out, and_5_out, not_1_out, not_2_out, not_3_out, not_4_out;

  not not_1 (not_1_out, A3);
  not not_2 (not_2_out, A2);
  not not_3 (not_3_out, A0);
  not not_4 (not_4_out, A3);
  and and_1 (and_1_out, not_1_out, A1);
  and and_2 (and_2_out, not_2_out, A1);
  or or_1 (S1, and_1_out, and_2_out, and_3_out);
  and and_3 (and_3_out, A1, not_3_out);
  and and_4 (and_4_out, not_4_out, A0);
  or or_2 (S0, and_4_out, and_5_out);
  and and_5 (and_5_out, A2, A1, A0);

  assign S2 = A2;
  assign S3 = 1'b0;
  assign VAI1 = A3;
endmodule

module comparador (
  input  [3:0] CHUTE_X,
  input  [3:0] CHUTE_Y,
  input  [3:0] X,
  input  [3:0] Y,
  input  CLK,
  output IGUAL,
  output SOMA_MAIOR,
  output SOMA_IGUAL,
  output SOMA_MENOR
);

  wire and_1_out, comparator_1_eq, comparator_2_eq, comparator_3_eq, comparator_3_gt, comparator_3_lt;
  wire [4:0] adder_1_out, adder_2_out, bit_extender_1_out, bit_extender_2_out, bit_extender_3_out,
       bit_extender_4_out;

  assign bit_extender_1_out = {{1{CHUTE_X[3]}}, CHUTE_X};  // Bit_Extender bit_extender_1
  assign bit_extender_2_out = {{1{CHUTE_Y[3]}}, CHUTE_Y};  // Bit_Extender bit_extender_2
  Comparator #(.width(4)) comparator_1 (.a(CHUTE_X), .b(X), .eq(comparator_1_eq));  // open: gt, lt
  Comparator #(.width(4)) comparator_2 (.a(CHUTE_Y), .b(Y), .eq(comparator_2_eq));  // open: gt, lt
  assign bit_extender_3_out = {{1{X[3]}}, X};  // Bit_Extender bit_extender_3
  assign bit_extender_4_out = {{1{Y[3]}}, Y};  // Bit_Extender bit_extender_4
  Adder #(.width(5)) adder_1 (.a(bit_extender_3_out), .b(bit_extender_4_out), .out(adder_1_out));  // open: cin, cout
  Adder #(.width(5)) adder_2 (.a(bit_extender_1_out), .b(bit_extender_2_out), .out(adder_2_out));  // open: cin, cout
  and and_1 (and_1_out, comparator_1_eq, comparator_2_eq);
  Comparator #(.width(5)) comparator_3 (
    .a(adder_2_out), .b(adder_1_out), .gt(comparator_3_gt), .eq(comparator_3_eq), .lt(comparator_3_lt));
  D_Flip_Flop d_ff_1 (.clk(CLK), .D(and_1_out), .Q(IGUAL));  // open: Qn, preset, en, reset
  D_Flip_Flop d_ff_2 (.clk(CLK), .D(comparator_3_gt), .Q(SOMA_MAIOR));  // open: Qn, preset, en, reset
  D_Flip_Flop d_ff_3 (.clk(CLK), .D(comparator_3_eq), .Q(SOMA_IGUAL));  // open: Qn, preset, en, reset
  D_Flip_Flop d_ff_4 (.clk(CLK), .D(comparator_3_lt), .Q(SOMA_MENOR));  // open: Qn, preset, en, reset
endmodule

module flip_flop_T (
  input  D,
  input  CLEAR,
  output Q,
  output Q_prime
);

  T_Flip_Flop t_ff_1 (.clk(D), .T(1'b1), .Q(Q), .Qn(Q_prime), .reset(CLEAR));  // open: preset, en
endmodule

module coordenadas (
  input  RESET,
  output [3:0] X,
  output [3:0] Y
);

  wire and_1_out, not_1_out, not_2_out, not_3_out;

  not not_1 (not_1_out, RESET);
  not not_2 (not_2_out, not_3_out);
  not not_3 (not_3_out, not_1_out);
  and and_1 (and_1_out, not_2_out, RESET);
  Random #(.width(4)) random_1 (.clk(and_1_out), .out(X));  // open: next, clr
  Random #(.width(4), .seed(64)) random_2 (.clk(and_1_out), .out(Y));  // open: next, clr
endmodule

module chuteXY (
  input  [3:0] CHUTEA,
  input  [3:0] CHUTEB,
  input  CLK,
  input  SELETOR_COO,
  input  SELETOR_JOG,
  output XS,
  output [3:0] X,
  output YS,
  output [3:0] Y,
  output [3:0] XCOMP2,
  output [3:0] YCOMP2
);

  wire and_1_out, and_2_out, and_3_out, not_1_out, not_2_out, not_3_out;
  wire [3:0] multiplexer_1_out;

  Multiplexer #(.width(4)) multiplexer_1 (
    .in0(CHUTEA), .in1(CHUTEB), .out(multiplexer_1_out), .sel(SELETOR_JOG));  // open: en
  not not_1 (not_1_out, not_2_out);
  not not_2 (not_2_out, CLK);
  not not_3 (not_3_out, not_1_out);
  and and_1 (and_1_out, not_3_out, CLK);
  Register #(.width(4)) u_X (.D(multiplexer_1_out), .Q(XCOMP2), .clk(and_2_out));  // open: en, clr
  and and_2 (and_2_out, and_1_out, ~SELETOR_COO);  // AND_Gate
  Register #(.width(4)) u_Y (.D(multiplexer_1_out), .Q(YCOMP2), .clk(and_3_out));  // open: en, clr
  and and_3 (and_3_out, and_1_out, SELETOR_COO);
  decode_comp2 decode_comp2_1 (
    .A3(XCOMP2[3]), .A2(XCOMP2[2]), .A1(XCOMP2[1]), .A0(XCOMP2[0]), .out_5(X));  // open: out_6
  decode_comp2 decode_comp2_2 (
    .A3(YCOMP2[3]), .A2(YCOMP2[2]), .A1(YCOMP2[1]), .A0(YCOMP2[0]), .out_5(Y));  // open: out_6

  assign XS = XCOMP2[3];
  assign YS = YCOMP2[3];
endmodule

module decode_coordenada (
  input  Q,
  output X,
  output Y
);

  not not_1 (X, Q);

  assign Y = Q;
endmodule

module decode_jogador (
  input  Q,
  output J_A,
  output J_B
);

  not not_1 (J_A, Q);

  assign J_B = Q;
endmodule

module decode_comp2 (
  input  A3,
  input  A2,
  input  A1,
  input  A0,
  output [3:0] out_5,
  output [3:0] out_6
);

  wire and_2_out, and_3_out, and_4_out, and_5_out, and_6_out, and_7_out, and_8_out, not_1_out, not_2_out,
       not_3_out, not_4_out, not_5_out, not_6_out, not_7_out, not_8_out, not_9_out, not_10_out, not_11_out;

  not not_1 (not_1_out, A2);
  not not_2 (not_2_out, A1);
  not not_3 (not_3_out, A0);
  not not_4 (not_4_out, A3);
  not not_5 (not_5_out, A1);
  not not_6 (not_6_out, A0);
  not not_7 (not_7_out, A2);
  not not_8 (not_8_out, A2);
  not not_9 (not_9_out, A3);
  not not_10 (not_10_out, A0);
  not not_11 (not_11_out, A1);
  and and_1 (out_5[3], A3, not_1_out, not_2_out, not_3_out);
  and and_2 (and_2_out, not_4_out, A2);
  and and_3 (and_3_out, A2, not_5_out, not_6_out);
  and and_4 (and_4_out, A3, not_7_out, A0);
  and and_5 (and_5_out, A3, not_8_out, A1);
  and and_6 (and_6_out, not_9_out, A1);
  and and_7 (and_7_out, A1, not_10_out);
  and and_8 (and_8_out, A3, not_11_out, A0);
  or or_1 (out_5[2], and_2_out, and_3_out, and_4_out, and_5_out);
  or or_2 (out_5[1], and_6_out, and_7_out, and_8_out);

  assign out_5[0] = A0;
  assign out_6 = {A3, A2, A1, A0};
endmodule

module game_core (
  input  [3:0] CHUTE_X,
  input  [3:0] CHUTE_Y,
  input  CHUTAR,
  input  RESET,
  input  TROCAR,
  input  SALVAR,
  output [3:0] PTA,
  output [3:0] PTB
);

  wire and_1_out, and_2_out, CHUTANDO_X, CHUTANDO_Y, flip_flop_t_1_q, flip_flop_t_2_q, IGUAL, or_1_out,
       or_3_out, RESET_t, SOMA_IGUAL, SOMA_MAIOR, SOMA_MENOR, TURNO_A, TURNO_B;
  wire [3:0] MAGIC_X, MAGIC_Y;

  or or_1 (or_1_out, TROCAR, SALVAR);
  flip_flop_T flip_flop_t_1 (.D(CHUTAR), .Q(flip_flop_t_1_q));  // open: Q_prime, CLEAR
  comparador comparador_1 (
    .CHUTE_X(CHUTE_X), .CHUTE_Y(CHUTE_Y), .X(MAGIC_X), .Y(MAGIC_Y), .CLK(CHUTAR), .IGUAL(IGUAL),
    .SOMA_MAIOR(SOMA_MAIOR), .SOMA_IGUAL(SOMA_IGUAL), .SOMA_MENOR(SOMA_MENOR));
  or or_2 (RESET_t, RESET, or_3_out);
  flip_flop_T flip_flop_t_2 (.D(or_1_out), .Q(flip_flop_t_2_q), .CLEAR(RESET_t));  // open: Q_prime
  decode_jogador decode_jogador_1 (.Q(flip_flop_t_1_q), .J_A(TURNO_A), .J_B(TURNO_B));
  decode_coordenada decode_coordenada_1 (.Q(flip_flop_t_2_q), .X(CHUTANDO_X), .Y(CHUTANDO_Y));
  and and_1 (and_1_out, IGUAL, TURNO_A);
  and and_2 (and_2_out, IGUAL, TURNO_B);
  Counter #(.width(4), .max('hf)) PONTOS_A (.count(and_1_out), .Q(PTA), .clk(and_1_out));  // open: load, D, carry, clr
  Counter #(.width(4), .max('hf)) PONTOS_B (.count(and_2_out), .Q(PTB), .clk(and_2_out));  // open: load, D, carry, clr
  or or_3 (or_3_out, and_1_out, and_2_out);
  coordenadas coordenadas_1 (.RESET(RESET_t), .X(MAGIC_X), .Y(MAGIC_Y));
endmodule
